// Logisim project Lab 2 Given.circ as structural Verilog: 7 circuits, main circuit Main
module Main (
);

  wire alu_1_zero, ALUsrc, Branch, clock_1_out, Jump, MemRead, MemToReg, MemWrite, R, RegDist, RegWrite;
  wire [1:0] OP;
  wire [2:0] alufunc_1_out2;
  wire [4:0] multiplexer_1_out;
  wire [7:0] bit_extender_1_out, bit_extender_3_out;
  wire [31:0] adder_2_out, alu_1_aluresult, bit_extender_2_out, multiplexer_2_out, multiplexer_3_out,
       multiplexer_4_out, multiplexer_5_out, PC_q, ram_1_data, register_file_1_rddata1,
       register_file_1_rddata2, rom_1_data, S, shifter_1_out;

  Clock clock_1 (.out(clock_1_out));
  Register #(.width(32)) PC (.D(multiplexer_4_out), .Q(PC_q), .clk(clock_1_out));  // open: en, clr
  Bit_Extender #(.in_width(32), .out_width(8)) bit_extender_1 (.in(PC_q), .out(bit_extender_1_out));
  Adder #(.width(32)) adder_1 (.a(32'h4), .b(PC_q), .out(S));  // open: cin, cout
  // Probe on nothing
  // Probe on nothing
  // Probe on nothing
  // Probe on nothing
  // Probe on nothing
  // Probe on nothing
  // Probe on nothing
  // Probe on nothing
  // Probe on nothing
  // Probe on nothing
  ROM #(.dataWidth(32)) rom_1 (.addr(bit_extender_1_out), .data(rom_1_data));  // open: sel
  Multiplexer #(.width(5), .enable("false")) multiplexer_1 (
    .in0(rom_1_data[15:11]), .in1(rom_1_data[20:16]), .out(multiplexer_1_out), .sel(RegDist));
  ControlUnit controlunit_1 (
    .In5(rom_1_data[26]), .In4(rom_1_data[27]), .In3(rom_1_data[28]), .In2(rom_1_data[29]),
    .In1(rom_1_data[30]), .In0(rom_1_data[31]), .RegDst(RegDist), .ALUSrc(ALUsrc), .MemToReg(MemToReg),
    .RegWrite(RegWrite), .MemRead(MemRead), .MemWrite(MemWrite), .Branch(Branch), .Jump(Jump),
    .ALUOp1(OP[1]), .ALUOp2(OP[0]));
  ALUFunc alufunc_1 (
    .Op1(OP[1]), .Op0(OP[0]), .In5(rom_1_data[0]), .In4(rom_1_data[1]), .In3(rom_1_data[2]),
    .In2(rom_1_data[3]), .In1(rom_1_data[4]), .In0(rom_1_data[5]), .Out2(alufunc_1_out2[0]),
    .Out1(alufunc_1_out2[1]), .Out0(alufunc_1_out2[2]));
  Register_File register_file_1 (
    .WrAddr(multiplexer_1_out), .WrData(multiplexer_5_out), .WrReg(RegWrite), .RdAddr1(rom_1_data[25:21]),
    .RdAddr2(rom_1_data[20:16]), .RdData1(register_file_1_rddata1), .RdData2(register_file_1_rddata2),
    .Clock(clock_1_out));
  assign bit_extender_2_out = {{16{1'b0}}, rom_1_data[15:0]};  // Bit_Extender bit_extender_2
  Multiplexer #(.width(32), .enable("false")) multiplexer_2 (
    .in0(register_file_1_rddata2), .in1(bit_extender_2_out), .out(multiplexer_2_out), .sel(ALUsrc));
  ALU alu_1 (
    .ALUCtl(alufunc_1_out2), .A(register_file_1_rddata1), .B(multiplexer_2_out), .ALUResult(alu_1_aluresult),
    .Zero(alu_1_zero), .Shamt({5{1'b0}}));  // open: Overflow
  Shifter #(.width(32)) shifter_1 (.in(bit_extender_2_out), .\dist (5'b00010), .out(shifter_1_out));
  and and_1 (R, Branch, alu_1_zero);
  Adder #(.width(32)) adder_2 (.a(shifter_1_out), .b(S), .out(adder_2_out));  // open: cin, cout
  Bit_Extender #(.in_width(32), .out_width(8)) bit_extender_3 (.in(alu_1_aluresult), .out(bit_extender_3_out));
  Multiplexer #(.width(32), .enable("false")) multiplexer_3 (
    .in0(shifter_1_out), .in1(adder_2_out), .out(multiplexer_3_out), .sel(R));
  Multiplexer #(.width(32), .enable("false")) multiplexer_4 (
    .in0(multiplexer_3_out), .in1(shifter_1_out), .out(multiplexer_4_out), .sel(Jump));
  RAM #(.dataWidth(32)) ram_1 (
    .addr(bit_extender_3_out), .data(ram_1_data), .clk(clock_1_out), .ld(MemRead));  // open: sel, clr
  Multiplexer #(.width(32), .enable("false")) multiplexer_5 (
    .in0(alu_1_aluresult), .in1(ram_1_data), .out(multiplexer_5_out), .sel(MemToReg));
endmodule

module ALU (
  input  [2:0] ALUCtl,
  input  [31:0] A,
  input  [31:0] B,
  input  [4:0] Shamt,
  output [31:0] ALUResult,
  output Zero,
  output Overflow
);

  wire comparator_1_lt, comparator_2_lt, comparator_3_eq, comparator_4_eq, or_2_out;
  wire [31:0] ADD, AND, NOR, OR, SLL, SLT, SLTU, SRL, SUB, XOR;

  // Probe on ALUCtl
  assign NOR = ~(A | B);  // NOR_Gate nor_1, 32 bits wide
  Adder #(.width(32)) adder_1 (.a(A), .b(B), .out(ADD));  // open: cin, cout
  Subtractor #(.width(32)) subtractor_1 (.a(A), .b(B), .out(SUB));  // open: bin, bout
  assign AND = A & B;  // AND_Gate and_1, 32 bits wide
  assign OR = A | B;  // OR_Gate or_1, 32 bits wide
  assign XOR = A ^ B;  // XOR_Gate xor_1, 32 bits wide
  Comparator #(.width(32)) comparator_1 (.a(A), .b(B), .lt(comparator_1_lt));  // open: gt, eq
  assign SLT = {{31{1'b0}}, comparator_1_lt};  // Bit_Extender bit_extender_1
  Shifter #(.width(32)) shifter_1 (.in(B), .\dist (Shamt), .out(SLL));
  Shifter #(.width(32), .shift("lr")) shifter_2 (.in(B), .\dist (Shamt), .out(SRL));
  Comparator #(.width(32), .mode("unsigned")) comparator_2 (.a(A), .b(B), .lt(comparator_2_lt));  // open: gt, eq
  assign SLTU = {{31{1'b0}}, comparator_2_lt};  // Bit_Extender bit_extender_2
  Multiplexer #(.select(3), .width(32), .enable("false")) multiplexer_1 (
    .in0(NOR), .in1(AND), .in2(SUB), .in3(SLT), .in4(OR), .in5(ADD), .out(ALUResult), .sel(ALUCtl));  // open: in6, in7
  Comparator #(.width(3)) comparator_3 (.a(3'b101), .b(ALUCtl), .eq(comparator_3_eq));  // open: gt, lt
  Comparator #(.width(3)) comparator_4 (.a(ALUCtl), .b(3'b010), .eq(comparator_4_eq));  // open: gt, lt
  Overflow_Unit overflow_unit_1 (
    .Add(comparator_3_eq), .Sub(comparator_4_eq), .ASign(A[31]), .BSign(B[31]), .ResultSign(ALUResult[31]),
    .Overflow(Overflow));
  not not_1 (Zero, or_2_out);
  or or_2 (or_2_out, ALUResult[0], ALUResult[1], ALUResult[2], ALUResult[3], ALUResult[4], ALUResult[5], ALUResult[6], ALUResult[7], ALUResult[8], ALUResult[9], ALUResult[10], ALUResult[11], ALUResult[12], ALUResult[13], ALUResult[14], ALUResult[15], ALUResult[16], ALUResult[17], ALUResult[18], ALUResult[19], ALUResult[20], ALUResult[21], ALUResult[22], ALUResult[23], ALUResult[24], ALUResult[25], ALUResult[26], ALUResult[27], ALUResult[28], ALUResult[29], ALUResult[30], ALUResult[31]);

  // Other names for the same wires on the sheet: ASign = A[31]; ResultSign = ALUResult[31]; BSign = B[31]

  // Notes on the sheet:
  //   ALUCtl for ADD for top port
  //   ALUCtl for SUB for second port
endmodule

module Register_File (
  input  [4:0] WrAddr,
  input  [31:0] WrData,
  input  WrReg,
  input  [4:0] RdAddr1,
  input  [4:0] RdAddr2,
  input  Clock,
  output [31:0] RdData1,
  output [31:0] RdData2
);

  wire WrReg0, WrReg1, WrReg2, WrReg3, WrReg4, WrReg5, WrReg6, WrReg7, WrReg8, WrReg9, WrReg10, WrReg11,
       WrReg12, WrReg13, WrReg14, WrReg15, WrReg16, WrReg17, WrReg18, WrReg19, WrReg20, WrReg21, WrReg22,
       WrReg23, WrReg24, WrReg25, WrReg26, WrReg27, WrReg28, WrReg29, WrReg30, WrReg31;
  wire [31:0] RegData1, RegData2, RegData3, RegData4, RegData5, RegData6, RegData7, RegData8, RegData9,
       RegData10, RegData11, RegData12, RegData13, RegData14, RegData15, RegData16, RegData17, RegData18,
       RegData19, RegData20, RegData21, RegData22, RegData23, RegData24, RegData25, RegData26, RegData27,
       RegData28, RegData29, RegData30, RegData31;

  Demultiplexer #(.select(5), .enable("false")) demultiplexer_1 (
    .out0(WrReg0), .out1(WrReg1), .out2(WrReg2), .out3(WrReg3), .out4(WrReg4), .out5(WrReg5), .out6(WrReg6),
    .out7(WrReg7), .out8(WrReg8), .out9(WrReg9), .out10(WrReg10), .out11(WrReg11), .out12(WrReg12),
    .out13(WrReg13), .out14(WrReg14), .out15(WrReg15), .out16(WrReg16), .out17(WrReg17), .out18(WrReg18),
    .out19(WrReg19), .out20(WrReg20), .out21(WrReg21), .out22(WrReg22), .out23(WrReg23), .out24(WrReg24),
    .out25(WrReg25), .out26(WrReg26), .out27(WrReg27), .out28(WrReg28), .out29(WrReg29), .out30(WrReg30),
    .out31(WrReg31), .in(WrReg), .sel(WrAddr));
  // Probe on RegData4
  Register #(.width(32)) Reg4 (.D(WrData), .en(WrReg4), .Q(RegData4), .clk(Clock));  // open: clr
  // Probe on RegData8
  Register #(.width(32)) Reg8 (.D(WrData), .en(WrReg8), .Q(RegData8), .clk(Clock));  // open: clr
  // Probe on RegData12
  Register #(.width(32)) Reg12 (.D(WrData), .en(WrReg12), .Q(RegData12), .clk(Clock));  // open: clr
  // Probe on RegData16
  Register #(.width(32)) Reg16 (.D(WrData), .en(WrReg16), .Q(RegData16), .clk(Clock));  // open: clr
  // Probe on RegData20
  Register #(.width(32)) Reg20 (.D(WrData), .en(WrReg20), .Q(RegData20), .clk(Clock));  // open: clr
  // Probe on RegData24
  Register #(.width(32)) Reg24 (.D(WrData), .en(WrReg24), .Q(RegData24), .clk(Clock));  // open: clr
  // Probe on RegData28
  Register #(.width(32)) Reg28 (.D(WrData), .en(WrReg28), .Q(RegData28), .clk(Clock));  // open: clr
  Register #(.width(32)) Reg1 (.D(WrData), .en(WrReg1), .Q(RegData1), .clk(Clock));  // open: clr
  Register #(.width(32)) Reg5 (.D(WrData), .en(WrReg5), .Q(RegData5), .clk(Clock));  // open: clr
  Register #(.width(32)) Reg9 (.D(WrData), .en(WrReg9), .Q(RegData9), .clk(Clock));  // open: clr
  Register #(.width(32)) Reg13 (.D(WrData), .en(WrReg13), .Q(RegData13), .clk(Clock));  // open: clr
  Register #(.width(32)) Reg17 (.D(WrData), .en(WrReg17), .Q(RegData17), .clk(Clock));  // open: clr
  Register #(.width(32)) Reg21 (.D(WrData), .en(WrReg21), .Q(RegData21), .clk(Clock));  // open: clr
  Register #(.width(32)) Reg25 (.D(WrData), .en(WrReg25), .Q(RegData25), .clk(Clock));  // open: clr
  Register #(.width(32)) Reg29 (.D(WrData), .en(WrReg29), .Q(RegData29), .clk(Clock));  // open: clr
  // Probe on RegData1
  // Probe on RegData5
  // Probe on RegData9
  // Probe on RegData13
  // Probe on RegData17
  // Probe on RegData21
  // Probe on RegData25
  // Probe on RegData29
  // Probe on RegData2
  Register #(.width(32)) Reg2 (.D(WrData), .en(WrReg2), .Q(RegData2), .clk(Clock));  // open: clr
  // Probe on RegData6
  Register #(.width(32)) Reg6 (.D(WrData), .en(WrReg6), .Q(RegData6), .clk(Clock));  // open: clr
  // Probe on RegData10
  Register #(.width(32)) Reg10 (.D(WrData), .en(WrReg10), .Q(RegData10), .clk(Clock));  // open: clr
  // Probe on RegData14
  Register #(.width(32)) Reg14 (.D(WrData), .en(WrReg14), .Q(RegData14), .clk(Clock));  // open: clr
  // Probe on RegData18
  Register #(.width(32)) Reg18 (.D(WrData), .en(WrReg18), .Q(RegData18), .clk(Clock));  // open: clr
  // Probe on RegData22
  Register #(.width(32)) Reg22 (.D(WrData), .en(WrReg22), .Q(RegData22), .clk(Clock));  // open: clr
  // Probe on RegData26
  Register #(.width(32)) Reg26 (.D(WrData), .en(WrReg26), .Q(RegData26), .clk(Clock));  // open: clr
  // Probe on RegData30
  Register #(.width(32)) Reg30 (.D(WrData), .en(WrReg30), .Q(RegData30), .clk(Clock));  // open: clr
  // Probe on RegData3
  Register #(.width(32)) Reg3 (.D(WrData), .en(WrReg3), .Q(RegData3), .clk(Clock));  // open: clr
  // Probe on RegData7
  Register #(.width(32)) Reg7 (.D(WrData), .en(WrReg7), .Q(RegData7), .clk(Clock));  // open: clr
  // Probe on RegData11
  Register #(.width(32)) Reg11 (.D(WrData), .en(WrReg11), .Q(RegData11), .clk(Clock));  // open: clr
  // Probe on RegData15
  Register #(.width(32)) Reg15 (.D(WrData), .en(WrReg15), .Q(RegData15), .clk(Clock));  // open: clr
  // Probe on RegData19
  Register #(.width(32)) Reg19 (.D(WrData), .en(WrReg19), .Q(RegData19), .clk(Clock));  // open: clr
  // Probe on RegData23
  Register #(.width(32)) Reg23 (.D(WrData), .en(WrReg23), .Q(RegData23), .clk(Clock));  // open: clr
  // Probe on RegData27
  Register #(.width(32)) Reg27 (.D(WrData), .en(WrReg27), .Q(RegData27), .clk(Clock));  // open: clr
  // Probe on RegData31
  Register #(.width(32)) Reg31 (.D(WrData), .en(WrReg31), .Q(RegData31), .clk(Clock));  // open: clr
  Multiplexer #(.select(5), .width(32), .enable("false")) multiplexer_1 (
    .in0({32{1'b0}}), .in1(RegData1), .in2(RegData2), .in3(RegData3), .in4(RegData4), .in5(RegData5),
    .in6(RegData6), .in7(RegData7), .in8(RegData8), .in9(RegData9), .in10(RegData10), .in11(RegData11),
    .in12(RegData12), .in13(RegData13), .in14(RegData14), .in15(RegData15), .in16(RegData16),
    .in17(RegData17), .in18(RegData18), .in19(RegData19), .in20(RegData20), .in21(RegData21),
    .in22(RegData22), .in23(RegData23), .in24(RegData24), .in25(RegData25), .in26(RegData26),
    .in27(RegData27), .in28(RegData28), .in29(RegData29), .in30(RegData30), .in31(RegData31), .out(RdData1),
    .sel(RdAddr1));
  Multiplexer #(.select(5), .width(32), .enable("false")) multiplexer_2 (
    .in0({32{1'b0}}), .in1(RegData1), .in2(RegData2), .in3(RegData3), .in4(RegData4), .in5(RegData5),
    .in6(RegData6), .in7(RegData7), .in8(RegData8), .in9(RegData9), .in10(RegData10), .in11(RegData11),
    .in12(RegData12), .in13(RegData13), .in14(RegData14), .in15(RegData15), .in16(RegData16),
    .in17(RegData17), .in18(RegData18), .in19(RegData19), .in20(RegData20), .in21(RegData21),
    .in22(RegData22), .in23(RegData23), .in24(RegData24), .in25(RegData25), .in26(RegData26),
    .in27(RegData27), .in28(RegData28), .in29(RegData29), .in30(RegData30), .in31(RegData31), .out(RdData2),
    .sel(RdAddr2));
endmodule

module Overflow_Unit (
  input  Add,
  input  Sub,
  input  ASign,
  input  BSign,
  input  ResultSign,
  output Overflow
);

  wire and_1_out, and_2_out, or_1_out, xnor_1_out, xor_1_out, xor_2_out;

  xnor xnor_1 (xnor_1_out, ASign, BSign);
  xor xor_1 (xor_1_out, ASign, BSign);
  and and_1 (and_1_out, xnor_1_out, Add);
  and and_2 (and_2_out, xor_1_out, Sub);
  or or_1 (or_1_out, and_1_out, and_2_out);
  xor xor_2 (xor_2_out, ResultSign, ASign);
  and and_3 (Overflow, or_1_out, xor_2_out);

  // Notes on the sheet:
  //   Overflow occurs when doing addition and sign(A) == sign(B) && sign(result) != sign(A)
  //   Or
  //   Overflow occurs when doing subtraction and sign(A) != sign(B) && sign(result) != sign(A)
endmodule

module ALUControl (
  input  In0,
  input  In1,
  input  In2,
  input  In3,
  input  In4,
  input  In5,
  input  Op0,
  input  Op1,
  output Out0,
  output Out1,
  output Out2
);

  wire and_1_out, and_2_out, and_4_out, not_1_out, not_2_out, not_3_out, not_4_out, not_5_out, not_6_out;

  not not_1 (not_1_out, In5);
  and and_1 (and_1_out, not_1_out, not_2_out);
  not not_2 (not_2_out, Op0);
  not not_3 (not_3_out, Op0);
  and and_2 (and_2_out, not_3_out, Op1);
  not not_4 (not_4_out, In5);
  and and_3 (Out1, not_4_out, Op0);
  not not_5 (not_5_out, Op0);
  and and_4 (and_4_out, not_5_out, not_6_out);
  not not_6 (not_6_out, Op1);
  or or_1 (Out0, and_1_out, and_2_out);
  or or_2 (Out2, and_4_out, In4);
endmodule

module ControlUnit (
  input  In5,
  input  In4,
  input  In3,
  input  In2,
  input  In1,
  input  In0,
  output RegDst,
  output ALUSrc,
  output MemToReg,
  output RegWrite,
  output MemRead,
  output MemWrite,
  output Branch,
  output Jump,
  output ALUOp1,
  output ALUOp2
);

  wire and_3_out, and_4_out, and_5_out, and_9_out, and_10_out, and_11_out, not_1_out, not_2_out, not_3_out,
       not_4_out, not_5_out, not_6_out, not_7_out, not_8_out, not_9_out, not_10_out, not_11_out, not_12_out,
       not_13_out;

  not not_1 (not_1_out, In3);
  not not_2 (not_2_out, In1);
  or or_1 (ALUSrc, In1, In3);
  not not_3 (not_3_out, In2);
  not not_4 (not_4_out, In1);
  not not_5 (not_5_out, In1);
  not not_6 (not_6_out, In3);
  not not_7 (not_7_out, In3);
  and and_1 (MemWrite, In3, In1);
  not not_8 (not_8_out, In3);
  not not_9 (not_9_out, In0);
  not not_10 (not_10_out, In2);
  not not_11 (not_11_out, In1);
  not not_12 (not_12_out, In1);
  not not_13 (not_13_out, In1);
  and and_2 (RegDst, not_1_out, not_2_out);
  and and_3 (and_3_out, not_3_out, not_4_out);
  and and_4 (and_4_out, In3, not_5_out);
  and and_5 (and_5_out, In5, not_6_out);
  and and_6 (MemRead, In5, not_7_out);
  and and_7 (Branch, not_8_out, In2);
  and and_8 (Jump, In1, not_9_out);
  and and_9 (and_9_out, not_10_out, not_11_out);
  and and_10 (and_10_out, In3, not_12_out);
  and and_11 (and_11_out, In3, not_13_out);
  or or_2 (RegWrite, and_3_out, and_4_out, and_5_out);
  or or_3 (ALUOp1, and_9_out, and_10_out);
  or or_4 (ALUOp2, In2, and_11_out);

  assign MemToReg = In1;
endmodule

module ALUFunc (
  input  Op1,
  input  Op0,
  input  In5,
  input  In4,
  input  In3,
  input  In2,
  input  In1,
  input  In0,
  output Out2,
  output Out1,
  output Out0
);

  wire and_1_out, and_2_out, and_3_out, and_4_out, and_5_out, and_6_out, and_7_out, not_1_out, not_2_out,
       not_3_out, not_4_out, not_5_out, not_6_out, not_7_out, not_8_out, not_9_out, not_10_out, not_11_out,
       not_12_out, not_13_out, not_14_out;

  not not_1 (not_1_out, Op1);
  and and_1 (and_1_out, not_1_out, not_2_out);
  not not_2 (not_2_out, Op0);
  not not_3 (not_3_out, Op0);
  not not_4 (not_4_out, In2);
  and and_2 (and_2_out, not_3_out, not_4_out, not_5_out);
  not not_5 (not_5_out, In1);
  not not_6 (not_6_out, Op0);
  and and_3 (and_3_out, not_6_out, not_7_out, In0);
  not not_7 (not_7_out, In1);
  not not_8 (not_8_out, In2);
  and and_4 (and_4_out, Op1, not_8_out, In1);
  not not_9 (not_9_out, Op1);
  and and_5 (and_5_out, not_9_out, not_10_out);
  not not_10 (not_10_out, Op0);
  not not_11 (not_11_out, Op0);
  and and_6 (and_6_out, not_11_out, not_12_out, not_13_out);
  not not_12 (not_12_out, In1);
  not not_13 (not_13_out, In0);
  not not_14 (not_14_out, Op0);
  and and_7 (and_7_out, not_14_out, In3);
  or or_1 (Out2, and_1_out, and_2_out, and_3_out);
  or or_2 (Out1, Op0, and_4_out);
  or or_3 (Out0, and_5_out, and_6_out, and_7_out);
endmodule
